// Logisim project muxrisccore.circ as structural Verilog: 1 circuit, main circuit main
module main (
);

  wire clock_1_out, comparator_1_eq;
  wire [15:0] counter_1_q;
  wire [63:0] ram_1_dout;

  Clock clock_1 (.out(clock_1_out));
  RAM #(.addrWidth(16), .dataWidth(64), .enables("line"), .trigger("falling"), .\type ("nonvolatile")) ram_1 (
    .addr(counter_1_q), .clk(clock_1_out), .dout(ram_1_dout));  // open: we, din
  Counter #(.max('hffff), .width(16)) counter_1 (
    .load(comparator_1_eq), .count(1'b1), .Q(counter_1_q), .up(1'b1), .clk(clock_1_out));  // open: D, carry, clr
  Comparator #(.width(64)) comparator_1 (.a(ram_1_dout), .b(64'h3), .eq(comparator_1_eq));  // open: gt, lt
  // Probe on ram_1_dout
endmodule
